# Fritzing sketch schematic (saved by Fritzing 1.0.5)

parts:
  F1 = FUSE [package=fuse_5mm]
  U3 = DC-DC_CONVERTER [package=dc-dc_converter]
  M1 = Niren can bus module [package=THT]
  Bauteil1 = Arduino Nano (Rev3.0)
  M2 = DC Motor [voltage_(max)=6V voltage_(min)=3V]  # not connected
  S1 = Pushbutton [package="[THT]"]  # not connected
  M3 = BTS7960  # not connected

nets:
  N1: F1.2, U3.VIN
  GND1: U3.GND1, M1.pin2, Bauteil1.GND
  N2: U3.VOUT, M1.pin1

custom parts:
  Niren can bus module: Niren can bus module availabe on ebay and others. Pcb view assumes that you unsolder the 7 pin header and resolder it on the bottom of the module to connect to the pcb. The two jumpers and the can bus connector remain on the top of the board and don't appear in pcb view.
  BTS7960: BTS7960 43A Peak Power H-Bridge PWM Motor Driver
